# Fritzing sketch esp32 (saved by Fritzing 0.9.3b)
breadboards: 1

parts:
  IC1 = DIP - 30 pins [chip_label=IC package="DIP (Dual Inline) [THT]"]
  M1 = fc-51 [package=THT]
  F1 = Fan - Ventilador [package=THT]
  R1 = PHOTOCELL [package=photocell-kit]
  R3 = Resistor [tolerance=±5% resistance=220 package="0805 [SMD]"]
  LED2 = LED - 5mm [color="Red (633nm)" package="5 mm [THT]"]
  R4 = Resistor [tolerance=±5% resistance=220 package="0805 [SMD]"]
  DHT1 = DHT11 Humitidy and Temperature Sensor (3 pins)
  Q1 = TRANSISTOR_NPN [package=to-92]
  VCC1 = Battery block 9V

nets:
  N1: IC1.3V3, M1.pin2, R1.P$1, DHT1.Plus
  GND: IC1.GND, M1.pin3, F1.GND, R3.Pin_1, LED2.anode, DHT1.Gnd, Q1.C
  N2: IC1.D2, R1.P$2, R3.Pin_0
  N3: IC1.D4, DHT1.Signal
  N4: IC1.D5, R4.Pin_0
  N5: IC1.D13, M1.pin1
  N6: IC1.VIN, Q1.E, VCC1.+
  N7: F1.5V, Q1.B
  N8: LED2.cathode, R4.Pin_1

custom parts:
  DIP - 30 pins: A DIP stand-in part for whatever IC you want. With 30 pins on a 300mil dual inline package (DIP) footprint.
  Fan - Ventilador: Ventilador de 2 pines, se encuentra comunmente en computadoras de escritorio
  DHT11 Humitidy and Temperature Sensor (3 pins): DHT11 Humidity and Temperature Sensor (3 pins).
